# Fritzing sketch mq131 (saved by Fritzing 0.9.4)
breadboards: 1

parts:
  U1 = GAS_SENSOR [package=mq-3]  # not connected
  Part1 = Adafruit Metro with Headers [part_number="Adafruit #2488"]
  LED1 = smd LED [color="Red (633nm)" package="1206 [SMD]"]
  R1 = Resistor [tolerance=±5% resistance=330 package="1206 [SMD]"]
  R2 = Resistor [tolerance=±5% resistance=10k package="1206 [SMD]"]

nets:
  N1: Part1.AD0, R2.Pin_0
  N2: Part1.MISO, Part1.SCK, Part1.RESET
  N3: Part1.VCCIO, Part1.MOSI, Part1.GND, R1.Pin_0, R2.Pin_1
  N4: LED1.cathode, R1.Pin_1

custom parts:
  Adafruit Metro with Headers: We sure love the ATmega328 here at Adafruit, and we use them a lot for our own projects. The processor has plenty of GPIO, Analog inputs, hardware UART SPI and I2C, timers and PWM galore - just enough for most simple projects. When we need to go small, we use a Pro Trinket 3V or 5V, but when size isn't as much of a concern, and an USB-serial converter is required, we reach for an Adafruit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
